# Fritzing sketch Receiver (saved by Fritzing 0.9.4)
breadboards: 1

parts:
  Компонент1 = LCD1602-I2C
  R1 = Photocell (LDR) [package=THT]
  R2 = Resistor [tolerance=±10% resistance=10k part_number=1 package="0805 [SMD]"]
  Компонент2 = Arduino Uno (Rev3)

nets:
  GND: Компонент1.GND, R2.Pin_0, Компонент2.GND
  N1: Компонент1.SDA, Компонент2.A4/SDA
  N2: Компонент1.SCL, Компонент2.A5/SCL
  N3: R1.pin_0, Компонент2.5V
  N4: R1.pin_1, R2.Pin_1, Компонент2.A0

custom parts:
  LCD1602-I2C: A standard character display, usually with 2x16 characters. Comes in many colors with LCM1602 IIC attached.
