# Fritzing sketch Transmitter (saved by Fritzing 0.9.4)

parts:
  Mod1 = KY-008 Laser Transmitter Module [package="Breakout board"]
  Компонент1 = Arduino Uno (Rev3)

nets:
  N1: Mod1.S, Компонент1.D13/SCK
  N2: Mod1.NC, Компонент1.3V3
  N3: Mod1.-, Компонент1.GND

custom parts:
  KY-008 Laser Transmitter Module: KY-008 Laser Transmitter Module, emits a dot shaped red laser beam.
